// Logisim project LE_FSM_pushbutton.circ as structural Verilog: 1 circuit, main circuit main
module main (
);

  wire and_1_out, and_2_out, and_3_out, d_ff_1_q, d_ff_2_q, HeartBeat_out, not_1_out, not_2_out, not_3_out,
       or_1_out, Push_out, xor_1_out;

  Button Push (.out(Push_out));
  not not_1 (not_1_out, d_ff_1_q);
  not not_2 (not_2_out, Push_out);
  not not_3 (not_3_out, d_ff_2_q);
  and and_1 (and_1_out, not_1_out, d_ff_2_q, not_2_out);
  and and_2 (and_2_out, d_ff_1_q, Push_out);
  and and_3 (and_3_out, d_ff_1_q, not_3_out);
  or or_1 (or_1_out, and_1_out, and_2_out, and_3_out);
  Clock HeartBeat (.out(HeartBeat_out));
  D_Flip_Flop d_ff_1 (.D(or_1_out), .clk(HeartBeat_out), .Q(d_ff_1_q));  // open: Qn, preset, reset
  D_Flip_Flop d_ff_2 (.D(Push_out), .clk(HeartBeat_out), .Q(d_ff_2_q));  // open: Qn, preset, reset
  xor xor_1 (xor_1_out, d_ff_1_q, d_ff_2_q);
  LED Lamp (.in(xor_1_out));
endmodule
